# Fritzing sketch ThermoCycler. (saved by Fritzing 0.9.4)
breadboards: 1

parts:
  Part1 = Arduino Nano (Rev3.0)
  Grove1 = Grove OLED 128x96
  F1 = Fan - Ventilador [package=THT]
  F2 = Fan - Ventilador [package=THT]
  Part2 = Adafruit Thermocouple Amplifier MAX31855 [part_number="Adafruit #269"]
  TIP41C_Transistor1 = TIP41C Transistor [package="TO220 [THT]"]  # not connected
  TIP41C_Transistor2 = TIP41C Transistor [package="TO220 [THT]"]  # not connected
  Power_plug1 = Power plug
  U1 = RELAY-SOLIDSTATE [package=relay-s108t02]
  Power_plug2 = Power plug

nets:
  GND: Part1.GND, Grove1.GND, Part2.GND, Power_plug1.GND, U1.+
  N1: Part1.D3, Part2.DO
  N2: Part1.D4, Part2.CS
  N3: Part1.D5, Part2.CLK
  N4: Part1.D11/MOSI, U1.-
  N5: Part1.A5, Grove1.SCL
  N6: Part1.A4, Grove1.SDA
  3V3: Part1.3V3, Grove1.VCC, Part2.VIN
  5V: F1.5V, F2.5V, Power_plug1.VCC
  N7: U1.T2, Power_plug2.GND

notes:
  Case Fan
  Fan on heatsink
  from 12v 500mA power supply
  Cartrige heater(s)
  12v 5A power supply
  To Thermocouple in the block

custom parts:
  Fan - Ventilador: Ventilador de 2 pines, se encuentra comunmente en computadoras de escritorio
  Adafruit Thermocouple Amplifier MAX31855: Thermocouples are very sensitive, requiring a good amplifier with a cold-compensation reference. The MAX31855K does everything for you, and can be easily interfaced with any microcontroller, even one without an analog input. This breakout board has the chip itself, a 3.3V regulator with 10uF bypass capacitors and level shifting circuitry, all assembled and tested. Comes with a 2 pin terminal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
  TIP41C Transistor: NPN Transistor.
